// Logisim project Traffic Light.circ as structural Verilog: 1 circuit, main circuit main
module main (
);

  wire and_1_out, clock_1_out, d_ff_1_q, d_ff_1_qn, d_ff_2_q, d_ff_2_qn;

  Clock #(.highDuration(5), .lowDuration(5)) clock_1 (.out(clock_1_out));
  D_Flip_Flop d_ff_1 (.clk(clock_1_out), .D(d_ff_1_qn), .Q(d_ff_1_q), .Qn(d_ff_1_qn));  // open: preset, en, reset
  D_Flip_Flop d_ff_2 (.clk(d_ff_1_qn), .D(d_ff_2_qn), .Q(d_ff_2_q), .Qn(d_ff_2_qn));  // open: preset, en, reset
  and and_1 (and_1_out, d_ff_1_qn, d_ff_2_q);
  LED led_1 (.in(d_ff_2_qn));
  LED led_2 (.in(d_ff_1_q));
  LED led_3 (.in(and_1_out));

  // Notes on the sheet:
  //   Clock receives Input to shift lights
  //   Clock
  //   Traffic Light by using D type Flip flop
  //   D flip flop 1
  //   D flip flop 2
  //   AND gate
  //   As clock sets an inut, this flip flop, based on previous stored bit will decide the out put. In this case altering the "Ready" Signal and Diode C aka "GO"!
  //   As clock sets an input and the first D flip flop, this flip flop, based on previous stored bit will decide the out put. In this case altering the "Stop"
  //   4th Year Software Engineering
  //   Diode A
  //   Diode B
  //   Diode C
  //   Group Members
  //   Betelhem Dejene  ATE 8178/06
  //   Dagmawi Tsegaye  ATE 8192/06
  //   Natnael Moges  ATE 8163/06
  //   Robel Debebe  ATE 8168/06
  //   Temesgen Endakmew  ATE 8289/06
  //   This AND gate receives bits from all three, the two flip flops and the clock, to alter the "GO!" diode, aka DIODE C
endmodule
